# Fritzing sketch LEDStatusIndicatorSmallHoles (saved by Fritzing 0.8.3b)
circuit board: 2.3cm x 2.64cm
breadboards: 1

parts:
  C1 = Electrolytic Capacitor [capacitance=100µF package="100 mil [THT, electrolytic]"]
  LED = RGB LED (com. anode, rbg) [package="5 mm [THT]"]
  R1 = Resistor [tolerance=±5% resistance=10k package=THT]
  R2 = Resistor [tolerance=±5% resistance=510 package=THT]
  R2_2 = Resistor [tolerance=±5% resistance=220 package=THT]
  R2_3 = Resistor [tolerance=±5% resistance=220 package=THT]
  VCC = Battery
  U1 = ATTINY45 [package=dip]
  S1 = Pushbutton [package="[THT]"]

nets:
  N1: C1.-, LED.blue_cathode, VCC.-, U1.GND, S1.Pin_1, S1.Pin_2
  N2: C1.+, R1.Pin_1, VCC.+, U1.VCC
  N3: LED.red_cathode, R2_2.Pin_0
  N4: LED.common_anode, R2_3.Pin_0
  N5: LED.green_cathode, R2.Pin_0
  N6: R1.Pin_0, U1.PB5(NRES)
  N7: R2.Pin_1, U1.PB4(ADC2)
  N8: R2_2.Pin_1, U1.PB0(MOSI)
  N9: R2_3.Pin_1, U1.PB1(MISO)
  N10: U1.PB3(ADC3), S1.Pin_3, S1.Pin_4

notes:
  Pato &
  Will
  LEDStatusIndicator
